// Logisim project FinalLab-AdjustedOutputs-Full.circ as structural Verilog: 1 circuit, main circuit main
module main (
  input  in_1,
  input  in_2,
  input  in_3
);

  wire and_1_out, and_2_out, and_3_out, and_4_out, and_5_out, clock_1_out, j_k_ff_1_q, j_k_ff_1_qn,
       j_k_ff_2_q, j_k_ff_2_qn, not_1_out, not_2_out, not_3_out, or_1_out, or_2_out, or_3_out, or_4_out;

  not not_1 (not_1_out, in_1);
  not not_2 (not_2_out, in_2);
  not not_3 (not_3_out, in_3);
  and and_1 (and_1_out, in_1, in_3, j_k_ff_2_q);
  or or_1 (or_1_out, not_3_out, not_1_out, j_k_ff_2_qn);
  and and_2 (and_2_out, in_1, in_3, j_k_ff_1_qn);
  or or_2 (or_2_out, j_k_ff_1_q, in_3);
  Clock clock_1 (.out(clock_1_out));
  J_K_Flip_Flop j_k_ff_1 (
    .J(and_1_out), .clk(clock_1_out), .K(or_1_out), .Q(j_k_ff_1_q), .Qn(j_k_ff_1_qn));  // open: preset, en, reset
  J_K_Flip_Flop j_k_ff_2 (
    .J(and_2_out), .clk(clock_1_out), .K(or_2_out), .Q(j_k_ff_2_q), .Qn(j_k_ff_2_qn));  // open: preset, en, reset
  and and_3 (and_3_out, in_1, not_3_out);
  and and_4 (and_4_out, j_k_ff_1_q, j_k_ff_2_qn);
  or or_3 (or_3_out, in_3, not_2_out);
  and and_5 (and_5_out, in_1, in_2, j_k_ff_1_q, j_k_ff_2_qn);
  or or_4 (or_4_out, and_3_out, and_4_out);
endmodule
