// Logisim project FinalLab-AdjustedOutputs.circ as structural Verilog: 1 circuit, main circuit main
module main (
  input  x1,
  input  x2,
  input  x3,
  input  y1,
  input  y2,
  output Y1_2,
  output Y2_2
);

  wire and_1_out, and_2_out, and_3_out, not_1_out, not_2_out, not_3_out, not_4_out;

  not not_1 (not_1_out, y2);
  not not_2 (not_2_out, x2);
  not not_3 (not_3_out, y1);
  not not_4 (not_4_out, y1);
  and and_1 (and_1_out, x2, x3, y1, not_1_out);
  and and_2 (and_2_out, x1, not_2_out, x3, y2);
  and and_3 (and_3_out, x1, x3, not_3_out, y2);
  and and_4 (Y2_2, x1, x3, not_4_out);
  or or_1 (Y1_2, and_1_out, and_2_out, and_3_out);
endmodule
