// Logisim project FinalLab-Outs.circ as structural Verilog: 2 circuits, main circuit main
module main (
  input  x1,
  input  x2,
  input  x3,
  input  y1,
  input  y2,
  input  y3,
  output Y1_2,
  output Y2_2,
  output Y3_2
);

  wire and_1_out, and_2_out, not_1_out, not_2_out, not_3_out;

  not not_1 (not_1_out, y2);
  not not_2 (not_2_out, y3);
  not not_3 (not_3_out, y3);
  and and_1 (and_1_out, x1, x3, not_1_out, y3);
  and and_2 (and_2_out, x1, x3, y2, not_2_out);
  and and_3 (Y3_2, x1, x3, not_3_out);
  or or_1 (Y2_2, and_1_out, and_2_out);

  assign Y1_2 = 1'b0;
endmodule

module Output (
  input  x1,
  input  x2,
  input  x3,
  input  y1,
  input  y2,
  input  y3,
  output z1,
  output z2,
  output z3
);

  wire and_2_out, and_3_out, not_1_out, not_2_out, not_3_out;

  not not_1 (not_1_out, x2);
  not not_2 (not_2_out, y2);
  not not_3 (not_3_out, y3);
  and and_1 (z2, x1, x3, y2, y3);
  and and_2 (and_2_out, x2, y2, y3);
  and and_3 (and_3_out, x1, x3, y2, y3);
  or or_1 (z1, not_1_out, not_2_out, not_3_out);
  or or_2 (z3, and_2_out, and_3_out);
endmodule
