// Logisim project finalLabMealy.circ as structural Verilog: 1 circuit, main circuit main
module main (
  input  N,
  input  B,
  input  L,
  output out_4,
  output out_5,
  output out_6,
  output out_7,
  output out_8
);

  wire and_1_out, and_2_out, and_3_out, and_4_out, and_6_out, and_7_out, clock_1_out, j_k_ff_1_qn,
       j_k_ff_2_qn, not_1_out, not_2_out, not_3_out, not_4_out, not_5_out, or_1_out, or_2_out;

  and and_1 (and_1_out, N, L, out_7);
  not not_1 (not_1_out, N);
  not not_2 (not_2_out, L);
  or or_1 (or_1_out, not_1_out, not_2_out, j_k_ff_2_qn);
  and and_2 (and_2_out, L, j_k_ff_1_qn, N);
  not not_3 (not_3_out, L);
  or or_2 (or_2_out, not_3_out, out_5);
  Clock clock_1 (.out(clock_1_out));
  J_K_Flip_Flop j_k_ff_1 (
    .J(and_1_out), .clk(clock_1_out), .K(or_1_out), .Q(out_5), .Qn(j_k_ff_1_qn));  // open: preset, en, reset
  J_K_Flip_Flop j_k_ff_2 (
    .J(and_2_out), .clk(clock_1_out), .K(or_2_out), .Q(out_7), .Qn(j_k_ff_2_qn));  // open: preset, en, reset
  and and_3 (and_3_out, L, out_7);
  and and_4 (and_4_out, j_k_ff_1_qn, L);
  not not_4 (not_4_out, B);
  and and_5 (out_6, N, L, out_5, j_k_ff_2_qn);
  and and_6 (and_6_out, N, not_5_out);
  not not_5 (not_5_out, L);
  and and_7 (and_7_out, out_5, j_k_ff_2_qn);
  or or_3 (out_4, and_3_out, and_4_out, not_4_out);
  or or_4 (out_8, and_6_out, and_7_out);
endmodule
