// Logisim project Part A - Adder.circ as structural Verilog: 1 circuit, main circuit main
module main (
  input  MSB,
  input  LSB,
  input  in_3,
  input  in_4,
  input  MSB_2,
  input  LSB_2,
  input  in_7,
  input  in_8
);

  wire [3:0] adder_1_out;

  Adder #(.width(4)) adder_1 (
    .a({in_4, MSB, LSB, in_3}), .b({in_8, MSB_2, LSB_2, in_7}), .out(adder_1_out));  // open: cin, cout
  LED led_1 (.in(adder_1_out[3]));
  LED led_2 (.in(adder_1_out[2]));
  LED led_3 (.in(adder_1_out[1]));
  LED led_4 (.in(adder_1_out[0]));

  // Notes on the sheet:
  //   Logical Diagram For A 3-Bit Full Adder
  //   Augend
  //   Addend
  //   Full Adder
endmodule
