// Logisim project Part A - Subtractor.circ as structural Verilog: 1 circuit, main circuit main
module main (
  input  MSB,
  input  LSB,
  input  in_3,
  input  in_4,
  input  MSB_2,
  input  LSB_2,
  input  in_7,
  input  in_8
);

  wire adder_1_cout;
  wire [2:0] not_3_out;
  wire [3:0] adder_1_out;

  not not_1 (not_3_out[1], LSB_2);
  not not_2 (not_3_out[2], MSB_2);
  not not_3 (not_3_out[0], in_7);
  Adder #(.width(4)) adder_1 (
    .a({in_4, MSB, LSB, in_3}), .b({in_8, not_3_out}), .out(adder_1_out), .cin(adder_1_cout),
    .cout(adder_1_cout));
  LED led_1 (.in(adder_1_out[3]));
  LED led_2 (.in(adder_1_out[2]));
  LED led_3 (.in(adder_1_out[0]));
  LED led_4 (.in(adder_1_out[1]));

  // Notes on the sheet:
  //   Minuend (A)
  //   Subtrahend (B)
  //   Logical Diagram For A 3-Bit Subtractor Using A Full Adder
  //   Full Adder
endmodule
