// Logisim project Lab5.circ as structural Verilog: 1 circuit, main circuit main
module main (
  input  Clock,
  input  in_2,
  input  in_3,
  input  in_4,
  input  in_5,
  input  in_6
);

  wire clock_1_out, d_ff_1_q, d_ff_1_qn, j_k_ff_1_q, j_k_ff_1_qn, j_k_ff_2_q, j_k_ff_2_qn, j_k_ff_3_q,
       j_k_ff_3_qn, not_1_out;

  Clock clock_1 (.out(clock_1_out));
  J_K_Flip_Flop j_k_ff_1 (
    .J(in_2), .clk(clock_1_out), .K(in_3), .Q(j_k_ff_1_q), .Qn(j_k_ff_1_qn), .preset(Clock), .en(Clock),
    .reset(Clock));
  D_Flip_Flop d_ff_1 (
    .clk(clock_1_out), .D(in_4), .Q(d_ff_1_q), .Qn(d_ff_1_qn), .preset(Clock), .en(Clock), .reset(Clock));
  J_K_Flip_Flop j_k_ff_2 (
    .J(in_5), .clk(clock_1_out), .K(not_1_out), .Q(j_k_ff_2_q), .Qn(j_k_ff_2_qn), .preset(Clock), .en(Clock),
    .reset(Clock));
  not not_1 (not_1_out, in_5);
  J_K_Flip_Flop j_k_ff_3 (
    .J(in_6), .clk(clock_1_out), .K(in_6), .Q(j_k_ff_3_q), .Qn(j_k_ff_3_qn), .preset(Clock), .en(Clock),
    .reset(Clock));
  LED led_1 (.in(j_k_ff_1_q));
  LED led_2 (.in(j_k_ff_1_qn));
  LED led_3 (.in(d_ff_1_q));
  LED led_4 (.in(d_ff_1_qn));
  LED led_5 (.in(j_k_ff_2_q));
  LED led_6 (.in(j_k_ff_2_qn));
  LED led_7 (.in(j_k_ff_3_q));
  LED led_8 (.in(j_k_ff_3_qn));

  // Notes on the sheet:
  //   Part A - JK Flip Flop
  //   Part B - D Flip Flop
  //   Enable - Preset - Clear
  //   Enable - Preset - Clear
  //   Part C - JK Flip Flop as a D Flip Flop
  //   Enable - Preset - Clear
  //   Part D - JK Flip Flop as a Toggle Flip Flop
  //   Enable - Preset - Clear
endmodule
