// Logisim project Lab 7.circ as structural Verilog: 1 circuit, main circuit main
module main (
  input  in_1,
  input  in_2,
  input  in_3,
  input  in_4
);

  wire and_1_out, and_2_out, clock_1_out, clock_2_out, j_k_ff_1_q, j_k_ff_1_qn, j_k_ff_2_q, j_k_ff_2_qn,
       j_k_ff_3_q, j_k_ff_4_q, j_k_ff_5_q, j_k_ff_5_qn, j_k_ff_6_q, not_1_out;

  Clock clock_1 (.out(clock_1_out));
  Clock clock_2 (.out(clock_2_out));
  J_K_Flip_Flop j_k_ff_1 (
    .J(in_1), .clk(clock_1_out), .K(in_1), .Q(j_k_ff_1_q), .Qn(j_k_ff_1_qn), .preset(and_2_out), .en(in_2));  // open: reset
  J_K_Flip_Flop j_k_ff_2 (
    .J(in_1), .clk(j_k_ff_1_q), .K(in_1), .Q(j_k_ff_2_q), .Qn(j_k_ff_2_qn), .preset(and_2_out), .en(in_2));  // open: reset
  LED led_1 (.in(j_k_ff_5_qn));
  J_K_Flip_Flop j_k_ff_3 (.J(in_3), .clk(clock_2_out), .K(in_3), .Q(j_k_ff_3_q));  // open: Qn, preset, en, reset
  LED led_2 (.in(j_k_ff_1_qn));
  LED led_3 (.in(j_k_ff_2_qn));
  J_K_Flip_Flop j_k_ff_4 (
    .J(j_k_ff_3_q), .clk(clock_2_out), .K(j_k_ff_3_q), .Q(j_k_ff_4_q));  // open: Qn, preset, en, reset
  LED led_4 (.in(j_k_ff_4_q));
  LED led_5 (.in(j_k_ff_6_q));
  J_K_Flip_Flop j_k_ff_5 (
    .J(in_1), .clk(j_k_ff_2_q), .K(in_1), .Q(j_k_ff_5_q), .Qn(j_k_ff_5_qn), .preset(and_2_out), .en(in_2));  // open: reset
  and and_1 (and_1_out, j_k_ff_4_q, j_k_ff_3_q);
  LED led_6 (.in(j_k_ff_3_q));
  not not_1 (not_1_out, j_k_ff_5_q);
  and and_2 (and_2_out, j_k_ff_1_q, j_k_ff_2_q, not_1_out);
  J_K_Flip_Flop j_k_ff_6 (
    .J(and_1_out), .clk(clock_2_out), .K(and_1_out), .Q(j_k_ff_6_q));  // open: Qn, preset, en, reset
endmodule
